// Logisim project p3.circ as structural Verilog: 7 circuits, main circuit main
module main (
  input  Reset,
  output [31:0] Instr,
  output RegWrite,
  output [4:0] RegAddr,
  output [31:0] RegData,
  output MemWrite,
  output [4:0] MemAddr,
  output [31:0] MemData
);

  wire alu_1_zero, clock_1_out, control_1_alusrc, control_1_branch, control_1_mem2reg, control_1_regdst;
  wire [1:0] control_1_extop_0;
  wire [2:0] control_1_aluop_0;
  wire [26:0] alu_1_result;
  wire [31:0] dm_1_read_result, ext_1_result, multiplexer_2_out, rf_1_read_result1;

  Clock clock_1 (.out(clock_1_out));
  // Probe on Instr
  ifu ifu_1 (.clk(clock_1_out), .rst(Reset), .branch(control_1_branch), .zero(alu_1_zero), .curr_instr(Instr));
  control control_1 (
    .curr_instr(Instr), .RegDst(control_1_regdst), .ALUSrc(control_1_alusrc), .Mem2Reg(control_1_mem2reg),
    .RegWrite(RegWrite), .MemWrite(MemWrite), .Branch(control_1_branch), .ExtOp_1(control_1_extop_0[1]),
    .ExtOp_0(control_1_extop_0[0]), .AluOp_2(control_1_aluop_0[2]), .AluOp_1(control_1_aluop_0[1]),
    .AluOp_0(control_1_aluop_0[0]));
  // Probe on Instr[25:21]
  // Probe on Instr[20:16]
  // Probe on RegAddr
  Multiplexer #(.width(5), .enable("false")) multiplexer_1 (
    .in0(Instr[15:11]), .in1(Instr[20:16]), .out(RegAddr), .sel(control_1_regdst));
  rf rf_1 (
    .read_addr1(Instr[25:21]), .read_addr2(Instr[20:16]), .write_addr(RegAddr), .write_data(RegData),
    .read_result1(rf_1_read_result1), .read_result2(MemData), .clk(clock_1_out), .rst(Reset),
    .write_enable(RegWrite));
  ext ext_1 (.num(Instr[15:0]), .mode(control_1_extop_0), .result(ext_1_result));
  Multiplexer #(.width(32), .enable("false")) multiplexer_2 (
    .in0(MemData), .in1(ext_1_result), .out(multiplexer_2_out), .sel(control_1_alusrc));
  alu alu_1 (
    .num1(rf_1_read_result1), .num2(multiplexer_2_out), .op(control_1_aluop_0),
    .result({alu_1_result[26:2], MemAddr, alu_1_result[1:0]}), .zero(alu_1_zero));  // open: comp_result, sig_comp_result
  dm dm_1 (
    .clk(clock_1_out), .rst(Reset), .addr({alu_1_result[26:2], MemAddr, alu_1_result[1:0]}),
    .write_data(MemData), .write_enable(MemWrite), .read_result(dm_1_read_result));
  Multiplexer #(.width(32), .enable("false")) multiplexer_3 (
    .in0({alu_1_result[26:2], MemAddr, alu_1_result[1:0]}), .in1(dm_1_read_result), .out(RegData),
    .sel(control_1_mem2reg));
endmodule

module rf (
  input  clk,
  input  rst,
  input  write_enable,
  input  [4:0] read_addr1,
  input  [4:0] read_addr2,
  input  [4:0] write_addr,
  input  [31:0] write_data,
  output [31:0] read_result1,
  output [31:0] read_result2
);

  wire we_0, we_1, we_2, we_3, we_4, we_5, we_6, we_7, we_8, we_9, we_10, we_11, we_12, we_13, we_14, we_15,
       we_16, we_17, we_18, we_19, we_20, we_21, we_22, we_23, we_24, we_25, we_26, we_27, we_28, we_29,
       we_30, we_31;
  wire [31:0] rd_1, rd_2, rd_3, rd_4, rd_5, rd_6, rd_7, rd_8, rd_9, rd_10, rd_11, rd_12, rd_13, rd_14, rd_15,
       rd_16, rd_17, rd_18, rd_19, rd_20, rd_21, rd_22, rd_23, rd_24, rd_25, rd_26, rd_27, rd_28, rd_29,
       rd_30, rd_31;

  Register #(.width(32)) register_1 (.D(write_data), .en(we_1), .Q(rd_1), .clk(clk), .clr(rst));
  Register #(.width(32)) register_2 (.D(write_data), .en(we_2), .Q(rd_2), .clk(clk), .clr(rst));
  Register #(.width(32)) register_3 (.D(write_data), .en(we_3), .Q(rd_3), .clk(clk), .clr(rst));
  Register #(.width(32)) register_4 (.D(write_data), .en(we_4), .Q(rd_4), .clk(clk), .clr(rst));
  Register #(.width(32)) register_5 (.D(write_data), .en(we_5), .Q(rd_5), .clk(clk), .clr(rst));
  Register #(.width(32)) register_6 (.D(write_data), .en(we_6), .Q(rd_6), .clk(clk), .clr(rst));
  Register #(.width(32)) register_7 (.D(write_data), .en(we_7), .Q(rd_7), .clk(clk), .clr(rst));
  Demultiplexer #(.select(5), .enable("false")) demultiplexer_1 (
    .out0(we_0), .out1(we_1), .out2(we_2), .out3(we_3), .out4(we_4), .out5(we_5), .out6(we_6), .out7(we_7),
    .out8(we_8), .out9(we_9), .out10(we_10), .out11(we_11), .out12(we_12), .out13(we_13), .out14(we_14),
    .out15(we_15), .out16(we_16), .out17(we_17), .out18(we_18), .out19(we_19), .out20(we_20), .out21(we_21),
    .out22(we_22), .out23(we_23), .out24(we_24), .out25(we_25), .out26(we_26), .out27(we_27), .out28(we_28),
    .out29(we_29), .out30(we_30), .out31(we_31), .in(write_enable), .sel(write_addr));
  Register #(.width(32)) register_8 (.D(write_data), .en(we_8), .Q(rd_8), .clk(clk), .clr(rst));
  Register #(.width(32)) register_9 (.D(write_data), .en(we_9), .Q(rd_9), .clk(clk), .clr(rst));
  Register #(.width(32)) register_10 (.D(write_data), .en(we_10), .Q(rd_10), .clk(clk), .clr(rst));
  Register #(.width(32)) register_11 (.D(write_data), .en(we_11), .Q(rd_11), .clk(clk), .clr(rst));
  Register #(.width(32)) register_12 (.D(write_data), .en(we_12), .Q(rd_12), .clk(clk), .clr(rst));
  Register #(.width(32)) register_13 (.D(write_data), .en(we_13), .Q(rd_13), .clk(clk), .clr(rst));
  Register #(.width(32)) register_14 (.D(write_data), .en(we_14), .Q(rd_14), .clk(clk), .clr(rst));
  Register #(.width(32)) register_15 (.D(write_data), .en(we_15), .Q(rd_15), .clk(clk), .clr(rst));
  Register #(.width(32)) register_16 (.D(write_data), .en(we_16), .Q(rd_16), .clk(clk), .clr(rst));
  Register #(.width(32)) register_17 (.D(write_data), .en(we_17), .Q(rd_17), .clk(clk), .clr(rst));
  Register #(.width(32)) register_18 (.D(write_data), .en(we_18), .Q(rd_18), .clk(clk), .clr(rst));
  Register #(.width(32)) register_19 (.D(write_data), .en(we_19), .Q(rd_19), .clk(clk), .clr(rst));
  Register #(.width(32)) register_20 (.D(write_data), .en(we_20), .Q(rd_20), .clk(clk), .clr(rst));
  Register #(.width(32)) register_21 (.D(write_data), .en(we_21), .Q(rd_21), .clk(clk), .clr(rst));
  Register #(.width(32)) register_22 (.D(write_data), .en(we_22), .Q(rd_22), .clk(clk), .clr(rst));
  Register #(.width(32)) register_23 (.D(write_data), .en(we_23), .Q(rd_23), .clk(clk), .clr(rst));
  Register #(.width(32)) register_24 (.D(write_data), .en(we_24), .Q(rd_24), .clk(clk), .clr(rst));
  Register #(.width(32)) register_25 (.D(write_data), .en(we_25), .Q(rd_25), .clk(clk), .clr(rst));
  Register #(.width(32)) register_26 (.D(write_data), .en(we_26), .Q(rd_26), .clk(clk), .clr(rst));
  Register #(.width(32)) register_27 (.D(write_data), .en(we_27), .Q(rd_27), .clk(clk), .clr(rst));
  Register #(.width(32)) register_28 (.D(write_data), .en(we_28), .Q(rd_28), .clk(clk), .clr(rst));
  Register #(.width(32)) register_29 (.D(write_data), .en(we_29), .Q(rd_29), .clk(clk), .clr(rst));
  Register #(.width(32)) register_30 (.D(write_data), .en(we_30), .Q(rd_30), .clk(clk), .clr(rst));
  Register #(.width(32)) register_31 (.D(write_data), .en(we_31), .Q(rd_31), .clk(clk), .clr(rst));
  Multiplexer #(.select(5), .width(32), .enable("false")) multiplexer_1 (
    .in0({32{1'b0}}), .in1(rd_1), .in2(rd_2), .in3(rd_3), .in4(rd_4), .in5(rd_5), .in6(rd_6), .in7(rd_7),
    .in8(rd_8), .in9(rd_9), .in10(rd_10), .in11(rd_11), .in12(rd_12), .in13(rd_13), .in14(rd_14),
    .in15(rd_15), .in16(rd_16), .in17(rd_17), .in18(rd_18), .in19(rd_19), .in20(rd_20), .in21(rd_21),
    .in22(rd_22), .in23(rd_23), .in24(rd_24), .in25(rd_25), .in26(rd_26), .in27(rd_27), .in28(rd_28),
    .in29(rd_29), .in30(rd_30), .in31(rd_31), .out(read_result1), .sel(read_addr1));
  Multiplexer #(.select(5), .width(32), .enable("false")) multiplexer_2 (
    .in0({32{1'b0}}), .in1(rd_1), .in2(rd_2), .in3(rd_3), .in4(rd_4), .in5(rd_5), .in6(rd_6), .in7(rd_7),
    .in8(rd_8), .in9(rd_9), .in10(rd_10), .in11(rd_11), .in12(rd_12), .in13(rd_13), .in14(rd_14),
    .in15(rd_15), .in16(rd_16), .in17(rd_17), .in18(rd_18), .in19(rd_19), .in20(rd_20), .in21(rd_21),
    .in22(rd_22), .in23(rd_23), .in24(rd_24), .in25(rd_25), .in26(rd_26), .in27(rd_27), .in28(rd_28),
    .in29(rd_29), .in30(rd_30), .in31(rd_31), .out(read_result2), .sel(read_addr2));

  // Other names for the same wires on the sheet: A1[4:0] = read_addr1; A2[4:0] = read_addr2; wd[31:0] = write_data;
  //   WE = write_enable
endmodule

module ext (
  input  [15:0] num,
  input  [1:0] mode,
  output [31:0] result
);

  wire [31:0] bit_extender_1_out, bit_extender_2_out, bit_extender_3_out, shifter_1_out;

  assign bit_extender_1_out = {{16{1'b0}}, num};  // Bit_Extender bit_extender_1
  assign bit_extender_2_out = {{16{num[15]}}, num};  // Bit_Extender bit_extender_2
  assign bit_extender_3_out = {{16{1'b0}}, num};  // Bit_Extender bit_extender_3
  Shifter #(.width(32)) shifter_1 (.in(bit_extender_3_out), .\dist (5'b10000), .out(shifter_1_out));
  Multiplexer #(.select(2), .width(32), .enable("false")) multiplexer_1 (
    .in0(bit_extender_1_out), .in1(bit_extender_2_out), .in2(shifter_1_out), .out(result), .sel(mode));  // open: in3
endmodule

module alu (
  input  [31:0] num1,
  input  [31:0] num2,
  input  [2:0] op,
  output [31:0] result,
  output [1:0] comp_result,
  output [1:0] sig_comp_result,
  output zero
);

  wire comparator_1_lt;
  wire [31:0] adder_1_out, and_1_out, bit_extender_1_out, not_1_out, or_1_out, subtractor_1_out;

  Adder #(.width(32)) adder_1 (.a(num1), .b(num2), .out(adder_1_out));  // open: cin, cout
  Subtractor #(.width(32)) subtractor_1 (.a(num1), .b(num2), .out(subtractor_1_out));  // open: bin, bout
  assign not_1_out = ~num1;  // NOT_Gate not_1, 32 bits wide
  Comparator #(.width(32)) comparator_1 (.a(num1), .b(num2), .lt(comparator_1_lt));  // open: gt, eq
  Comparator #(.width(32)) comparator_2 (
    .a(num1), .b(num2), .gt(sig_comp_result[1]), .lt(sig_comp_result[0]));  // open: eq
  Comparator #(.width(32)) comparator_3 (.a(num1), .b(num2), .gt(comp_result[1]), .lt(comp_result[0]));  // open: eq
  assign and_1_out = num1 & num2;  // AND_Gate and_1, 32 bits wide
  assign or_1_out = num1 | num2;  // OR_Gate or_1, 32 bits wide
  assign bit_extender_1_out = {{31{1'b0}}, comparator_1_lt};  // Bit_Extender bit_extender_1
  Multiplexer #(.select(3), .width(32), .enable("false")) multiplexer_1 (
    .in0(adder_1_out), .in1(subtractor_1_out), .in2(and_1_out), .in3(or_1_out), .in4(not_1_out),
    .in5(bit_extender_1_out), .out(result), .sel(op));  // open: in6, in7
  Comparator #(.width(32)) comparator_4 (.a(subtractor_1_out), .b({32{1'b0}}), .eq(zero));  // open: gt, lt

  // Notes on the sheet:
  //   2comp
  //   2comp
  //   unsig
endmodule

module dm (
  input  clk,
  input  rst,
  input  [31:0] addr,
  input  [31:0] write_data,
  input  write_enable,
  output [31:0] read_result
);

  RAM #(.addrWidth(5), .dataWidth(32), .bus("separate")) ram_1 (
    .addr(addr[6:2]), .din(write_data), .data(read_result), .str(write_enable), .clk(clk), .ld(1'b1),
    .clr(rst));  // open: sel
endmodule

module control (
  input  [31:0] curr_instr,
  output RegDst,
  output ALUSrc,
  output Mem2Reg,
  output RegWrite,
  output MemWrite,
  output Branch,
  output ExtOp_1,
  output ExtOp_0,
  output AluOp_2,
  output AluOp_1,
  output AluOp_0
);

  wire and_1_out, and_2_out, comparator_1_eq, comparator_2_eq, comparator_3_eq, comparator_4_eq,
       comparator_5_eq, comparator_6_eq, comparator_7_eq, comparator_8_eq;

  Comparator #(.width(6), .mode("unsigned")) comparator_1 (
    .a(curr_instr[5:0]), .b(6'b100001), .eq(comparator_1_eq));  // open: gt, lt
  Comparator #(.width(6), .mode("unsigned")) comparator_2 (
    .a(curr_instr[5:0]), .b(6'b100011), .eq(comparator_2_eq));  // open: gt, lt
  Comparator #(.width(6), .mode("unsigned")) comparator_3 (
    .a(curr_instr[31:26]), .b({6{1'b0}}), .eq(comparator_3_eq));  // open: gt, lt
  Comparator #(.width(6), .mode("unsigned")) comparator_4 (
    .a(curr_instr[31:26]), .b(6'b001111), .eq(comparator_4_eq));  // open: gt, lt
  Comparator #(.width(6), .mode("unsigned")) comparator_5 (
    .a(curr_instr[31:26]), .b(6'b001101), .eq(comparator_5_eq));  // open: gt, lt
  Comparator #(.width(6), .mode("unsigned")) comparator_6 (
    .a(curr_instr[31:26]), .b(6'b100011), .eq(comparator_6_eq));  // open: gt, lt
  Comparator #(.width(6), .mode("unsigned")) comparator_7 (
    .a(curr_instr[31:26]), .b(6'b101011), .eq(comparator_7_eq));  // open: gt, lt
  Comparator #(.width(6), .mode("unsigned")) comparator_8 (
    .a(curr_instr[31:26]), .b(6'b000100), .eq(comparator_8_eq));  // open: gt, lt
  and and_1 (and_1_out, comparator_1_eq, comparator_3_eq);
  and and_2 (and_2_out, comparator_2_eq, comparator_3_eq);
  or or_1 (RegDst, comparator_4_eq, comparator_5_eq, comparator_6_eq);
  or or_2 (ALUSrc, comparator_4_eq, comparator_5_eq, comparator_6_eq, comparator_7_eq);
  buf or_3 (Mem2Reg, comparator_6_eq);  // OR_Gate
  or or_4 (RegWrite, and_1_out, and_2_out, comparator_4_eq, comparator_5_eq, comparator_6_eq);
  buf or_5 (MemWrite, comparator_7_eq);  // OR_Gate
  buf or_6 (Branch, comparator_8_eq);  // OR_Gate
  buf or_7 (ExtOp_1, comparator_4_eq);  // OR_Gate
  or or_8 (ExtOp_0, comparator_6_eq, comparator_7_eq);
  buf or_9 (AluOp_2, 1'b0);  // OR_Gate
  or or_10 (AluOp_1, comparator_4_eq, comparator_5_eq);
  or or_11 (AluOp_0, comparator_5_eq, and_2_out, comparator_4_eq);

  // Notes on the sheet:
  //   lui
  //   ori
  //   lw
  //   sw
  //   beq
  //   addu
  //   subu
  //   lui
  //   ori
  //   lw
  //   sw
  //   beq
endmodule

module ifu (
  input  clk,
  input  rst,
  input  branch,
  input  zero,
  output [31:0] curr_instr
);

  wire and_1_out;
  wire [31:0] adder_1_out, adder_2_out, bit_extender_1_out, multiplexer_1_out, pc_q;

  and and_1 (and_1_out, branch, zero);
  Multiplexer #(.width(32), .enable("false")) multiplexer_1 (
    .in0(adder_2_out), .in1(adder_1_out), .out(multiplexer_1_out), .sel(and_1_out));
  Adder #(.width(32)) adder_1 (.a(adder_2_out), .b(bit_extender_1_out), .out(adder_1_out));  // open: cin, cout
  Register #(.width(32)) pc (.D(multiplexer_1_out), .Q(pc_q), .clk(clk), .clr(rst));  // open: en
  Adder #(.width(32)) adder_2 (.a(pc_q), .b(32'h1), .out(adder_2_out));  // open: cin, cout
  ROM #(.addrWidth(5), .dataWidth(32)) rom_1 (.addr(pc_q[4:0]), .data(curr_instr));  // open: sel
  assign bit_extender_1_out = {{16{curr_instr[15]}}, curr_instr[15:0]};  // Bit_Extender bit_extender_1

  // Notes on the sheet:
  //   contents of rom_1 (hex, n*v repeats v):
  //   34210002 34420002 221821 3c04ffff 3484ffff 42823 ac010004 8c060004 10850002 3c07dead 3c08beef
  //   10000001 3529babe 1021fffe
endmodule
