// Logisim project fib2.circ as structural Verilog: 6 circuits, main circuit main
module main (
  input  [31:0] N,
  output [31:0] Nth
);

  wire clk, comparator_1_gt, got_one_bit_q, not_1_out, not_2_out, register_1_q;
  wire [4:0] counter_1_q;
  wire [31:0] and_1_out, decoder_1_out31, multiplexer_1_out, multiplexer_2_out, multiplexer_3_out,
       multiplexer_4_out, step_1_o00, step_1_o01, step_1_o10, step_1_o11, step_pff_1_o00, step_pff_1_o01,
       step_pff_1_o10, step_pff_1_o11;

  Clock clock_1 (.out(clk));
  Counter #(.width(5), .max('h1f), .ongoal("stay")) counter_1 (
    .Q(counter_1_q), .clk(clk));  // open: load, D, count, carry, clr
  Register #(.width(1)) got_one_bit (.D(1'b1), .en(comparator_1_gt), .Q(got_one_bit_q), .clk(clk));  // open: clr
  Decoder #(.select(5), .enable("false")) decoder_1 (
    .out0(decoder_1_out31[31]), .out1(decoder_1_out31[30]), .out2(decoder_1_out31[29]),
    .out3(decoder_1_out31[28]), .out4(decoder_1_out31[27]), .out5(decoder_1_out31[26]),
    .out6(decoder_1_out31[25]), .out7(decoder_1_out31[24]), .out8(decoder_1_out31[23]),
    .out9(decoder_1_out31[22]), .out10(decoder_1_out31[21]), .out11(decoder_1_out31[20]),
    .out12(decoder_1_out31[19]), .out13(decoder_1_out31[18]), .out14(decoder_1_out31[17]),
    .out15(decoder_1_out31[16]), .out16(decoder_1_out31[15]), .out17(decoder_1_out31[14]),
    .out18(decoder_1_out31[13]), .out19(decoder_1_out31[12]), .out20(decoder_1_out31[11]),
    .out21(decoder_1_out31[10]), .out22(decoder_1_out31[9]), .out23(decoder_1_out31[8]),
    .out24(decoder_1_out31[7]), .out25(decoder_1_out31[6]), .out26(decoder_1_out31[5]),
    .out27(decoder_1_out31[4]), .out28(decoder_1_out31[3]), .out29(decoder_1_out31[2]),
    .out30(decoder_1_out31[1]), .out31(decoder_1_out31[0]), .sel(counter_1_q));
  assign and_1_out = N & decoder_1_out31;  // AND_Gate and_1, 32 bits wide
  Register #(.width(1)) register_1 (.D(decoder_1_out31[0]), .en(1'b1), .Q(register_1_q), .clk(clk));  // open: clr
  not not_1 (not_1_out, register_1_q);
  Comparator #(.width(32), .mode("unsigned")) comparator_1 (
    .a(and_1_out), .b({32{1'b0}}), .gt(comparator_1_gt));  // open: eq, lt
  step step_1 (
    .i00(step_pff_1_o00), .i01(step_pff_1_o01), .i10(step_pff_1_o10), .i11(step_pff_1_o11),
    .curr_bit(comparator_1_gt), .o00(step_1_o00), .o01(step_1_o01), .o10(step_1_o10), .o11(step_1_o11));
  not not_2 (not_2_out, got_one_bit_q);
  Multiplexer #(.width(32), .enable("false")) multiplexer_1 (
    .in0(step_1_o00), .in1(32'h1), .out(multiplexer_1_out), .sel(not_2_out));
  Multiplexer #(.width(32), .enable("false")) multiplexer_2 (
    .in0(step_1_o01), .in1(32'h1), .out(multiplexer_2_out), .sel(not_2_out));
  Multiplexer #(.width(32), .enable("false")) multiplexer_3 (
    .in0(step_1_o10), .in1(32'h1), .out(multiplexer_3_out), .sel(not_2_out));
  Multiplexer #(.width(32), .enable("false")) multiplexer_4 (
    .in0(step_1_o11), .in1(32'h1), .out(multiplexer_4_out), .sel(not_2_out));
  step_pff step_pff_1 (
    .i00(multiplexer_1_out), .i01(multiplexer_2_out), .i10(multiplexer_3_out), .i11(multiplexer_4_out),
    .en(not_1_out), .o00(step_pff_1_o00), .o01(step_pff_1_o01), .o10(step_pff_1_o10), .o11(step_pff_1_o11));
  Multiplexer #(.width(32), .enable("false")) multiplexer_5 (
    .in0(step_pff_1_o00), .in1({32{1'b0}}), .out(Nth), .sel(not_1_out));
  Multiplexer #(.width(32), .enable("false")) multiplexer_6 (
    .in0(step_pff_1_o01), .in1({32{1'b0}}), .sel(not_1_out));  // open: out
  Multiplexer #(.width(32), .enable("false")) multiplexer_7 (
    .in0(step_pff_1_o10), .in1({32{1'b0}}), .sel(not_1_out));  // open: out
  Multiplexer #(.width(32), .enable("false")) multiplexer_8 (
    .in0(step_pff_1_o11), .in1({32{1'b0}}), .sel(not_1_out));  // open: out
endmodule

module matrix_squaring (
  input  [31:0] i00,
  input  [31:0] i01,
  input  [31:0] i10,
  input  [31:0] i11,
  output [31:0] o00,
  output [31:0] o01,
  output [31:0] o10,
  output [31:0] o11
);

  wire [31:0] multiplier_1_out, multiplier_2_out, multiplier_3_out, multiplier_4_out, multiplier_5_out,
       multiplier_6_out, multiplier_7_out, multiplier_8_out;

  Multiplier #(.width(32)) multiplier_1 (.a(i00), .b(i00), .out(multiplier_1_out));  // open: cin, cout
  Multiplier #(.width(32)) multiplier_2 (.a(i01), .b(i10), .out(multiplier_2_out));  // open: cin, cout
  Multiplier #(.width(32)) multiplier_3 (.a(i00), .b(i01), .out(multiplier_3_out));  // open: cin, cout
  Multiplier #(.width(32)) multiplier_4 (.a(i01), .b(i11), .out(multiplier_4_out));  // open: cin, cout
  Multiplier #(.width(32)) multiplier_5 (.a(i00), .b(i10), .out(multiplier_5_out));  // open: cin, cout
  Multiplier #(.width(32)) multiplier_6 (.a(i10), .b(i11), .out(multiplier_6_out));  // open: cin, cout
  Multiplier #(.width(32)) multiplier_7 (.a(i01), .b(i10), .out(multiplier_7_out));  // open: cin, cout
  Multiplier #(.width(32)) multiplier_8 (.a(i11), .b(i11), .out(multiplier_8_out));  // open: cin, cout
  Adder #(.width(32)) adder_1 (.a(multiplier_1_out), .b(multiplier_2_out), .out(o00));  // open: cin, cout
  Adder #(.width(32)) adder_2 (.a(multiplier_3_out), .b(multiplier_4_out), .out(o01));  // open: cin, cout
  Adder #(.width(32)) adder_3 (.a(multiplier_5_out), .b(multiplier_6_out), .out(o10));  // open: cin, cout
  Adder #(.width(32)) adder_4 (.a(multiplier_7_out), .b(multiplier_8_out), .out(o11));  // open: cin, cout
endmodule

module matrix_squaring_with_orig (
  input  [31:0] i00,
  input  [31:0] i01,
  input  [31:0] i10,
  input  [31:0] i11,
  output [31:0] o00,
  output [31:0] o01,
  output [31:0] o10,
  output [31:0] o11
);

  wire [31:0] matrix_squaring_1_o01, matrix_squaring_1_o11;

  matrix_squaring matrix_squaring_1 (
    .i00(i00), .i01(i01), .i10(i10), .i11(i11), .o00(o01), .o01(matrix_squaring_1_o01), .o10(o11),
    .o11(matrix_squaring_1_o11));
  Adder #(.width(32)) adder_1 (.a(o01), .b(matrix_squaring_1_o01), .out(o00));  // open: cin, cout
  Adder #(.width(32)) adder_2 (.a(o11), .b(matrix_squaring_1_o11), .out(o10));  // open: cin, cout
endmodule

module step (
  input  [31:0] i00,
  input  [31:0] i01,
  input  [31:0] i10,
  input  [31:0] i11,
  input  curr_bit,
  output [31:0] o00,
  output [31:0] o01,
  output [31:0] o10,
  output [31:0] o11
);

  wire [31:0] matrix_squaring_1_o00, matrix_squaring_1_o01, matrix_squaring_1_o10, matrix_squaring_1_o11,
       matrix_squaring_with_orig_1_o00, matrix_squaring_with_orig_1_o01, matrix_squaring_with_orig_1_o10,
       matrix_squaring_with_orig_1_o11;

  matrix_squaring matrix_squaring_1 (
    .i00(i00), .i01(i01), .i10(i10), .i11(i11), .o00(matrix_squaring_1_o00), .o01(matrix_squaring_1_o01),
    .o10(matrix_squaring_1_o10), .o11(matrix_squaring_1_o11));
  matrix_squaring_with_orig matrix_squaring_with_orig_1 (
    .i00(i00), .i01(i01), .i10(i10), .i11(i11), .o00(matrix_squaring_with_orig_1_o00),
    .o01(matrix_squaring_with_orig_1_o01), .o10(matrix_squaring_with_orig_1_o10),
    .o11(matrix_squaring_with_orig_1_o11));
  Multiplexer #(.width(32), .enable("false")) multiplexer_1 (
    .in0(matrix_squaring_1_o00), .in1(matrix_squaring_with_orig_1_o00), .out(o00), .sel(curr_bit));
  Multiplexer #(.width(32), .enable("false")) multiplexer_2 (
    .in0(matrix_squaring_1_o01), .in1(matrix_squaring_with_orig_1_o01), .out(o01), .sel(curr_bit));
  Multiplexer #(.width(32), .enable("false")) multiplexer_3 (
    .in0(matrix_squaring_1_o10), .in1(matrix_squaring_with_orig_1_o10), .out(o10), .sel(curr_bit));
  Multiplexer #(.width(32), .enable("false")) multiplexer_4 (
    .in0(matrix_squaring_1_o11), .in1(matrix_squaring_with_orig_1_o11), .out(o11), .sel(curr_bit));
endmodule

module step_pff (
  input  [31:0] i00,
  input  [31:0] i01,
  input  [31:0] i10,
  input  [31:0] i11,
  input  en,
  output [31:0] o00,
  output [31:0] o01,
  output [31:0] o10,
  output [31:0] o11
);

  wire clock_1_out;

  Clock clock_1 (.out(clock_1_out));
  Register #(.width(32)) register_1 (.D(i00), .en(en), .Q(o00), .clk(clock_1_out));  // open: clr
  Register #(.width(32)) register_2 (.D(i01), .en(en), .Q(o01), .clk(clock_1_out));  // open: clr
  Register #(.width(32)) register_3 (.D(i10), .en(en), .Q(o10), .clk(clock_1_out));  // open: clr
  Register #(.width(32)) register_4 (.D(i11), .en(en), .Q(o11), .clk(clock_1_out));  // open: clr
endmodule

module orig_matrix (
  output [31:0] o00,
  output [31:0] o01,
  output [31:0] o10,
  output [31:0] o11
);


  assign o00 = 32'h1;
  assign o01 = 32'h1;
  assign o10 = 32'h1;
  assign o11 = {32{1'b0}};
endmodule
